# Fritzing sketch proyectoSETR (saved by Fritzing 0.9.2b)
breadboards: 2

parts:
  DHT1 = DHT11 Humitidy and Temperature Sensor
  Arduino1 = Arduino Uno (Rev3)
  LED1 = LED - 5mm [color="Green (560nm)" package="5 mm [THT]"]
  R1 = Trimmer Potentiometer [maximum_resistance=10kΩ package=THT]
  J1 = Piezo Speaker
  LED2 = LED - 5mm [color="Red (633nm)" package="5 mm [THT]"]
  LED3 = LED - 5mm [color="Green (560nm)" package="5 mm [THT]"]
  LED4 = LED - 5mm [color="Red (633nm)" package="5 mm [THT]"]
  R2 = Trimmer Potentiometer [maximum_resistance=10kΩ package=THT]
  R3 = Trimmer Potentiometer [maximum_resistance=10kΩ package=THT]
  J2 = Piezo Speaker
  U1 = microSD Socket [package=micro-sd-socket-pp]  # not connected
  TRXCOM1 = RJ45-TRXCOM [part_number=TRJ0011BANL]  # not connected
  R4 = Trimmer Potentiometer [maximum_resistance=10kΩ package=THT]

nets:
  VDD: DHT1.VDD, Arduino1.5V
  N1: DHT1.DATA, Arduino1.D7
  GND: DHT1.GND, Arduino1.GND, LED1.anode, LED2.anode, LED3.anode, LED4.anode
  N2: Arduino1.D2, R4.leg2
  N3: Arduino1.D3_PWM, J1.pin2
  N4: Arduino1.D4, J2.pin2
  N5: Arduino1.D5_PWM, R2.leg2
  N6: LED1.cathode, R4.wiper
  N7: R1.wiper, LED2.cathode
  N8: R1.leg2, J1.pin1
  N9: LED3.cathode, R2.wiper
  N10: LED4.cathode, R3.wiper
  N11: R3.leg2, J2.pin1

custom parts:
  DHT11 Humitidy and Temperature Sensor: DHT11 Humidity and Temperature Sensor
  RJ45-TRXCOM: RJ45 Connector with 10/100 Base-T Integrated Magnetics and 2 LED (TRJ0011BANL)
